// Logisim project project2.circ as structural Verilog: 21 circuits, main circuit main
// Subop
module main (
  input  in_1,
  output [1:0] ALUSrc,
  output [3:0] out_3,
  output [2:0] out_4,
  output [15:0] out_5,
  output [2:0] out_6,
  output [15:0] out_7,
  output [15:0] out_8,
  output [15:0] out_9
);

  wire addui, ALUSrc_t, Bn_out, Bp_out, Branch, branchcontrol_1_bn, branchcontrol_1_bp, branchcontrol_1_bx,
       branchcontrol_1_bz, Bx_out, Bz_out, Clock, clock_1_out, decoder_1_memread, decoder_1_memtoreg,
       decoder_1_memwrite, decoder_1_regwrite, Halt, hi_control_1_hi, hi_low_control_1_hi,
       immedcontrol_1_immed, JAL, jrcontrol_1_jump, jumpcontrol_1_jump, mult_divcontrol_1_multcontrol,
       multcontrol_1_multcontrol, not_1_out, not_2_out, or_1_out, putcontrol_1_put, Subop, SW, Zero;
  wire [3:0] multiplexer_9_out, multiplexer_9_out_2, multiplexer_9_out_3, multiplexer_9_out_4;
  wire [4:0] _8bitImmediate;
  wire [7:0] adder_1_out, multiplexer_7_out, multiplexer_10_out, multiplexer_13_out, PC_q;
  wire [15:0] address, alu_1_result, bit_extender_2_out, bit_extender_3_out, divider_1_out, divider_1_rem,
       jr, multiplexer_2_out, multiplexer_4_out, multiplexer_5_out, multiplexer_8_out, multiplexer_11_out,
       multiplexer_14_out, multiplexer_15_out, multiplier_1_cout, multiplier_1_out, PC_1, ram_1_data,
       registers_1_read_data_1, registers_1_read_data_2;

  Clock clock_1 (.out(clock_1_out));
  Multiplexer #(.enable("false")) multiplexer_1 (.in0(clock_1_out), .in1(1'b0), .out(Clock), .sel(Halt));
  Adder adder_1 (.a(PC_q), .b(8'h1), .out(adder_1_out), .cin(1'b0));  // open: cout
  Register PC (.D(multiplexer_13_out), .en(not_1_out), .Q(PC_q), .clk(Clock), .clr(in_1));
  not not_1 (not_1_out, Halt);
  SWControl swcontrol_1 (.Opcode(out_3), .ALUSrc(SW));
  JALControl jalcontrol_1 (.Opcode(out_3), .jump(JAL));
  ALUSrcControl alusrccontrol_1 (.Opcode(out_3), .subop(Subop), .alusrc(ALUSrc_t));
  adduiControl adduicontrol_1 (.Opcode(out_3), .subop(Subop), .addui(addui));
  assign PC_1 = {{8{1'b0}}, adder_1_out};  // Bit_Extender bit_extender_1
  ImmedControl immedcontrol_1 (.Opcode(out_3), .immed(immedcontrol_1_immed));
  ROM #(.dataWidth(16)) rom_1 (.addr(PC_q), .data({out_3, out_4, out_6, _8bitImmediate, Subop}), .sel(1'b1));
  Multiplexer #(.width(16), .enable("false")) multiplexer_2 (
    .in0(out_5), .in1(multiplexer_4_out), .out(multiplexer_2_out), .sel(immedcontrol_1_immed));
  LED u_HALT (.in(Halt));
  Decoder decoder_1 (
    .Opcode(out_3), .subop(Subop), .Branch(Branch), .MemRead(decoder_1_memread),
    .MemtoReg(decoder_1_memtoreg), .Halt(Halt), .MemWrite(decoder_1_memwrite), .RegWrite(decoder_1_regwrite));  // open: ALUSrc, Immed
  Multiplexer #(.width(16), .enable("false")) multiplexer_3 (
    .in0(multiplexer_2_out), .in1(PC_1), .out(out_7), .sel(JAL));
  Multiplexer #(.width(16), .enable("false")) multiplexer_4 (
    .in0(multiplexer_8_out), .in1(multiplexer_5_out), .out(multiplexer_4_out), .sel(hi_low_control_1_hi));
  Hi_Control hi_control_1 (.Opcode(out_3), .subop(Subop), .Hi(hi_control_1_hi));
  Hi_Low_Control hi_low_control_1 (.Opcode(out_3), .subop(Subop), .Hi(hi_low_control_1_hi));
  Multiplexer #(.width(16), .enable("false")) multiplexer_5 (
    .in0(out_9), .in1(out_8), .out(multiplexer_5_out), .sel(hi_control_1_hi));
  Hex_Digit_Display hex_digit_display_1 (.value(multiplexer_9_out_4));  // open: dp
  BranchControl branchcontrol_1 (
    .Opcode(out_3), .bp(branchcontrol_1_bp), .bn(branchcontrol_1_bn), .bx(branchcontrol_1_bx),
    .bz(branchcontrol_1_bz));
  ALUControl alucontrol_1 (.Opcode(out_3), .SubOp(Subop), .ALUControl(ALUSrc));
  Hex_Digit_Display hex_digit_display_2 (.value(multiplexer_9_out_3));  // open: dp
  not not_2 (not_2_out, Zero);
  Registers registers_1 (
    .writeEnable(decoder_1_regwrite), .Write_Register(out_4), .Read_Register_1(out_4),
    .Read_Register_2(out_6), .Write_Data(out_7), .Clock(Clock), .Read_Data_1(registers_1_read_data_1),
    .Read_Data_2(registers_1_read_data_2));
  Multiplexer #(.width(16), .enable("false")) multiplexer_6 (
    .in0(registers_1_read_data_2), .in1(multiplexer_8_out), .out(jr), .sel(ALUSrc_t));
  assign bit_extender_2_out = {{8{1'b0}}, {out_6, _8bitImmediate}};  // Bit_Extender bit_extender_2
  assign bit_extender_3_out = {{8{out_6[2]}}, {out_6, _8bitImmediate}};  // Bit_Extender bit_extender_3
  Hex_Digit_Display hex_digit_display_3 (.value(multiplexer_9_out_2));  // open: dp
  Multiplexer #(.width(8), .enable("false")) multiplexer_7 (
    .in0(adder_1_out), .in1({out_6, _8bitImmediate}), .out(multiplexer_7_out), .sel(or_1_out));
  and Bp (Bp_out, Branch, branchcontrol_1_bp);
  and Bn (Bn_out, Branch, branchcontrol_1_bn);
  or or_1 (or_1_out, Bp_out, Bn_out, Bx_out, Bz_out);
  and Bx (Bx_out, Branch, branchcontrol_1_bx, Zero);
  and Bz (Bz_out, Branch, branchcontrol_1_bz, not_2_out);
  Multiplexer #(.width(16), .enable("false")) multiplexer_8 (
    .in0(bit_extender_2_out), .in1(bit_extender_3_out), .out(multiplexer_8_out), .sel(addui));
  Hex_Digit_Display hex_digit_display_4 (.value(multiplexer_9_out));  // open: dp
  Multiplexer #(.width(16), .enable("false")) multiplexer_9 (
    .in0({16{1'b0}}), .in1(registers_1_read_data_1),
    .out({multiplexer_9_out_4, multiplexer_9_out_3, multiplexer_9_out_2, multiplexer_9_out}),
    .sel(putcontrol_1_put));
  ALU alu_1 (.A(registers_1_read_data_1), .B(jr), .Operation(ALUSrc), .Result(alu_1_result), .Zero(Zero));
  PutControl putcontrol_1 (.Opcode(out_3), .Put(putcontrol_1_put));
  Multiplexer #(.width(8), .enable("false")) multiplexer_10 (
    .in0(multiplexer_7_out), .in1({out_6, _8bitImmediate}), .out(multiplexer_10_out), .sel(jumpcontrol_1_jump));
  JumpControl jumpcontrol_1 (.Opcode(out_3), .jump(jumpcontrol_1_jump));
  Multiplexer #(.width(16), .enable("false")) multiplexer_11 (
    .in0(registers_1_read_data_2), .in1(registers_1_read_data_1), .out(multiplexer_11_out), .sel(SW));
  Multiplexer #(.width(16), .enable("false")) multiplexer_12 (
    .in0(alu_1_result), .in1(registers_1_read_data_2), .out(address), .sel(SW));
  Divider #(.width(16)) divider_1 (
    .a(registers_1_read_data_1), .b(jr), .out(divider_1_out), .rem(divider_1_rem));  // open: upper
  Multiplier #(.width(16)) multiplier_1 (
    .a(registers_1_read_data_1), .b(jr), .out(multiplier_1_out), .cout(multiplier_1_cout));  // open: cin
  Multiplexer #(.width(8), .enable("false")) multiplexer_13 (
    .in0(multiplexer_10_out), .in1(jr[7:0]), .out(multiplexer_13_out), .sel(jrcontrol_1_jump));
  multControl multcontrol_1 (.Opcode(out_3), .subop(Subop), .multcontrol(multcontrol_1_multcontrol));
  JRControl jrcontrol_1 (.Opcode(out_3), .jump(jrcontrol_1_jump));
  RAM #(.dataWidth(16), .bus("separate")) ram_1 (
    .addr(address[7:0]), .din(multiplexer_11_out), .data(ram_1_data), .str(decoder_1_memwrite), .sel(1'b1),
    .clk(Clock), .ld(decoder_1_memread));  // open: clr
  Multiplexer #(.width(16), .enable("false")) multiplexer_14 (
    .in0(divider_1_rem), .in1(multiplier_1_cout), .out(multiplexer_14_out), .sel(multcontrol_1_multcontrol));
  Multiplexer #(.width(16), .enable("false")) multiplexer_15 (
    .in0(divider_1_out), .in1(multiplier_1_out), .out(multiplexer_15_out), .sel(multcontrol_1_multcontrol));
  Multiplexer #(.width(16), .enable("false")) multiplexer_16 (
    .in0(alu_1_result), .in1(ram_1_data), .out(out_5), .sel(decoder_1_memtoreg));
  mult_divcontrol mult_divcontrol_1 (.Opcode(out_3), .multcontrol(mult_divcontrol_1_multcontrol));
  Register #(.width(16)) hi (
    .D(multiplexer_14_out), .en(mult_divcontrol_1_multcontrol), .Q(out_8), .clk(Clock));  // open: clr
  Register #(.width(16)) lo (
    .D(multiplexer_15_out), .en(mult_divcontrol_1_multcontrol), .Q(out_9), .clk(Clock));  // open: clr

  // Other names for the same wires on the sheet: rs[2:0] = out_4; Opcode[3:0] = out_3; _8bitImmediate[7:5] = out_6;
  //   rt[2:0] = out_6; data[15:0] = out_5; hi[15:0] = out_8; lo[15:0] = out_9; WriteData[15:0] = out_7

  // Notes on the sheet:
  //   PC in
  //   PC+4
  //   contents of rom_1 (hex, n*v repeats v):
  //   f016 f204 3040 a000 b000 a000
  //   Opcode
  //   Luke Kraus LEK81@Pitt.edu  3911602
  //   ALUConrol
  //   PCSrc
  //   MemWrite
  //   Write Data
  //   MemRead
  //   MemToReg
endmodule

module ALU (
  input  [15:0] A,
  input  [15:0] B,
  input  [1:0] Operation,
  output [15:0] Result,
  output Zero
);

  wire [15:0] adder_1_out, and_1_out, not_1_out, or_1_out, subtractor_1_out;

  Adder #(.width(16)) adder_1 (.a(A), .b(B), .out(adder_1_out), .cin(1'b0));  // open: cout
  Subtractor #(.width(16)) subtractor_1 (.a(A), .b(B), .out(subtractor_1_out), .bin(1'b0));  // open: bout
  assign or_1_out = A | B;  // OR_Gate or_1, 16 bits wide
  assign not_1_out = ~or_1_out;  // NOT_Gate not_1, 16 bits wide
  assign and_1_out = A & B;  // AND_Gate and_1, 16 bits wide
  Multiplexer #(.select(2), .width(16), .enable("false")) multiplexer_1 (
    .in0(adder_1_out), .in1(subtractor_1_out), .in2(not_1_out), .in3(and_1_out), .out(Result), .sel(Operation));
  or or_2 (Zero, A[0], A[1], A[2], A[3], A[4], A[5], A[6], A[7], A[8], A[9], A[10], A[11], A[12], A[13], A[14], A[15]);

  // Notes on the sheet:
  //   00 Is add, 01 is Sub, 10 is Nor, 11 is AND
endmodule

module Registers (
  input  writeEnable,
  input  [2:0] Write_Register,
  input  [2:0] Read_Register_1,
  input  [2:0] Read_Register_2,
  input  [15:0] Write_Data,
  input  Clock,
  output [15:0] Read_Data_1,
  output [15:0] Read_Data_2
);

  wire demultiplexer_1_out0, demultiplexer_1_out1, demultiplexer_1_out2, demultiplexer_1_out3,
       demultiplexer_1_out4, demultiplexer_1_out5, demultiplexer_1_out6, demultiplexer_1_out7;
  wire [15:0] r0_q, r1_q, r2_q, r3_q, r4_q, r5_q, r6_q, r7_q;

  Demultiplexer #(.select(3), .enable("false")) demultiplexer_1 (
    .out0(demultiplexer_1_out0), .out1(demultiplexer_1_out1), .out2(demultiplexer_1_out2),
    .out3(demultiplexer_1_out3), .out4(demultiplexer_1_out4), .out5(demultiplexer_1_out5),
    .out6(demultiplexer_1_out6), .out7(demultiplexer_1_out7), .in(writeEnable), .sel(Write_Register));
  Register #(.width(16)) r0 (.D(Write_Data), .en(demultiplexer_1_out0), .Q(r0_q), .clk(Clock));  // open: clr
  Register #(.width(16)) r1 (.D(Write_Data), .en(demultiplexer_1_out1), .Q(r1_q), .clk(Clock));  // open: clr
  Register #(.width(16)) r2 (.D(Write_Data), .en(demultiplexer_1_out2), .Q(r2_q), .clk(Clock));  // open: clr
  Register #(.width(16)) r3 (.D(Write_Data), .en(demultiplexer_1_out3), .Q(r3_q), .clk(Clock));  // open: clr
  Register #(.width(16)) r4 (.D(Write_Data), .en(demultiplexer_1_out4), .Q(r4_q), .clk(Clock));  // open: clr
  Register #(.width(16)) r5 (.D(Write_Data), .en(demultiplexer_1_out5), .Q(r5_q), .clk(Clock));  // open: clr
  Register #(.width(16)) r6 (.D(Write_Data), .en(demultiplexer_1_out6), .Q(r6_q), .clk(Clock));  // open: clr
  Register #(.width(16)) r7 (.D(Write_Data), .en(demultiplexer_1_out7), .Q(r7_q), .clk(Clock));  // open: clr
  Multiplexer #(.select(3), .width(16), .enable("false")) multiplexer_1 (
    .in0(r0_q), .in1(r1_q), .in2(r2_q), .in3(r3_q), .in4(r4_q), .in5(r5_q), .in6(r6_q), .in7(r7_q),
    .out(Read_Data_1), .sel(Read_Register_1));
  Multiplexer #(.select(3), .width(16), .enable("false")) multiplexer_2 (
    .in0(r0_q), .in1(r1_q), .in2(r2_q), .in3(r3_q), .in4(r4_q), .in5(r5_q), .in6(r6_q), .in7(r7_q),
    .out(Read_Data_2), .sel(Read_Register_2));

  // Notes on the sheet:
  //   This subcurcuit hold the registers for the project
  //   The mux can be used to choose which one is used
endmodule

module Decoder (
  input  [3:0] Opcode,
  input  subop,
  output Branch,
  output MemRead,
  output MemtoReg,
  output Halt,
  output MemWrite,
  output RegWrite,
  output ALUSrc,
  output Immed
);

  wire and_1_out, and_2_out, and_3_out, and_5_out, and_6_out, and_8_out, and_9_out, and_10_out, and_11_out,
       and_12_out, and_13_out, not_1_out, not_2_out, not_3_out, not_4_out, not_5_out, not_6_out, not_7_out,
       not_8_out, not_9_out, not_10_out, not_11_out, not_12_out, not_13_out, not_14_out, not_15_out,
       not_16_out, not_17_out, not_18_out, not_19_out, not_20_out, not_21_out;

  not not_1 (not_1_out, Opcode[3]);
  not not_2 (not_2_out, Opcode[3]);
  not not_3 (not_3_out, Opcode[2]);
  not not_4 (not_4_out, Opcode[1]);
  not not_5 (not_5_out, Opcode[0]);
  not not_6 (not_6_out, Opcode[1]);
  not not_7 (not_7_out, Opcode[0]);
  not not_8 (not_8_out, subop);
  not not_9 (not_9_out, Opcode[2]);
  not not_10 (not_10_out, Opcode[0]);
  not not_11 (not_11_out, Opcode[1]);
  not not_12 (not_12_out, Opcode[0]);
  not not_13 (not_13_out, Opcode[2]);
  not not_14 (not_14_out, Opcode[2]);
  not not_15 (not_15_out, Opcode[0]);
  not not_16 (not_16_out, Opcode[1]);
  not not_17 (not_17_out, Opcode[0]);
  not not_18 (not_18_out, Opcode[1]);
  not not_19 (not_19_out, Opcode[3]);
  not not_20 (not_20_out, Opcode[2]);
  not not_21 (not_21_out, Opcode[1]);
  and and_1 (and_1_out, not_1_out, Opcode[2], Opcode[0]);
  and and_2 (and_2_out, not_2_out, Opcode[2], Opcode[1]);
  and and_3 (and_3_out, Opcode[3], not_3_out, not_4_out, not_5_out);
  and and_4 (MemRead, Opcode[3], Opcode[2], not_6_out, not_7_out, not_8_out);
  and and_5 (and_5_out, Opcode[3], not_9_out, not_10_out);
  and and_6 (and_6_out, Opcode[3], not_11_out, not_12_out);
  and and_7 (Halt, Opcode[3], not_13_out, Opcode[1], Opcode[0]);
  and and_8 (and_8_out, Opcode[3], not_14_out, Opcode[1], not_15_out);
  and and_9 (and_9_out, Opcode[3], Opcode[2], not_16_out, not_17_out, subop);
  and and_10 (and_10_out, not_18_out, Opcode[0]);
  and and_11 (and_11_out, Opcode[2], Opcode[0]);
  and and_12 (and_12_out, not_19_out, Opcode[2], Opcode[1]);
  and and_13 (and_13_out, Opcode[3], not_20_out, not_21_out);
  or or_1 (Branch, and_1_out, and_2_out, and_3_out);
  or or_2 (MemtoReg, and_5_out, and_6_out);
  or or_3 (MemWrite, and_8_out, and_9_out);
  or or_4 (Immed, and_10_out, and_11_out, and_12_out, and_13_out);

  assign ALUSrc = 1'b0;
  assign RegWrite = 1'b1;
endmodule

module Fields (
  input  [15:0] Instruction,
  input  I,
  output out_3,
  output Subop,
  output [2:0] rt,
  output [2:0] rs,
  output [3:0] Opcode,
  output [7:0] immediate,
  output [2:0] rs_2
);

  wire [14:0] demultiplexer_1_out0;
  wire [15:0] demultiplexer_1_out1;

  Demultiplexer #(.width(16), .enable("false")) demultiplexer_1 (
    .out0({out_3, demultiplexer_1_out0[14:10], rt, rs, demultiplexer_1_out0[3:0]}),
    .out1({demultiplexer_1_out1[15], immediate, rs_2, demultiplexer_1_out1[3:0]}), .in(Instruction), .sel(I));
  Multiplexer #(.enable("false")) multiplexer_1 (.in0(out_3), .in1(demultiplexer_1_out1[15]), .out(Subop), .sel(I));
  Multiplexer #(.width(4), .enable("false")) multiplexer_2 (
    .in0(demultiplexer_1_out0[3:0]), .in1(demultiplexer_1_out1[3:0]), .out(Opcode), .sel(I));
endmodule

module ALUControl (
  input  [3:0] Opcode,
  input  SubOp,
  output [1:0] ALUControl
);

  wire and_1_out, and_2_out, and_3_out, and_4_out, and_5_out, not_1_out, not_2_out, not_3_out, not_4_out,
       not_5_out, not_6_out, not_7_out, not_8_out, not_9_out, not_10_out;

  not not_1 (not_1_out, Opcode[3]);
  not not_2 (not_2_out, Opcode[3]);
  not not_3 (not_3_out, Opcode[1]);
  not not_4 (not_4_out, Opcode[0]);
  not not_5 (not_5_out, Opcode[3]);
  not not_6 (not_6_out, Opcode[1]);
  not not_7 (not_7_out, Opcode[0]);
  not not_8 (not_8_out, Opcode[3]);
  not not_9 (not_9_out, Opcode[2]);
  not not_10 (not_10_out, SubOp);
  and and_1 (and_1_out, not_1_out, Opcode[1]);
  and and_2 (and_2_out, not_2_out, Opcode[2]);
  and and_3 (and_3_out, Opcode[3], not_3_out, not_4_out);
  and and_4 (and_4_out, not_5_out, not_6_out, not_7_out, SubOp);
  and and_5 (and_5_out, not_8_out, not_9_out, Opcode[1], not_10_out);
  or or_1 (ALUControl[1], and_1_out, and_2_out, and_3_out);
  or or_2 (ALUControl[0], and_4_out, and_5_out);
endmodule

module Control (
  input  [3:0] Opcode,
  input  SubOp,
  input  a0,
  input  a1,
  input  a2,
  input  a3,
  input  subop_2,
  output Branch,
  output MemRead,
  output MemtoReg,
  output Halt,
  output MemWrite,
  output RegWrite,
  output jump,
  output ALUSrc,
  output Immed
);

  wire and_1_out, and_2_out, and_3_out, and_8_out, and_9_out, and_10_out, and_11_out, and_12_out, and_13_out,
       and_14_out, and_15_out, and_16_out, and_17_out, and_18_out, and_19_out, and_20_out, and_21_out,
       and_22_out, not_1_out, not_2_out, not_3_out, not_4_out, not_5_out, not_6_out, not_7_out, not_8_out,
       not_9_out, not_10_out, not_11_out, not_12_out, not_13_out, not_14_out, not_15_out, not_16_out,
       not_17_out, not_18_out, not_19_out, not_20_out, not_21_out, not_22_out, not_23_out, not_24_out,
       not_25_out, not_26_out, not_27_out, not_28_out, not_29_out, not_30_out, not_31_out, not_32_out;

  not not_1 (not_1_out, Opcode[3]);
  not not_2 (not_2_out, Opcode[3]);
  not not_3 (not_3_out, Opcode[2]);
  not not_4 (not_4_out, Opcode[1]);
  not not_5 (not_5_out, Opcode[0]);
  not not_6 (not_6_out, Opcode[1]);
  not not_7 (not_7_out, Opcode[0]);
  not not_8 (not_8_out, SubOp);
  not not_9 (not_9_out, Opcode[1]);
  not not_10 (not_10_out, Opcode[0]);
  not not_11 (not_11_out, Opcode[2]);
  not not_12 (not_12_out, Opcode[1]);
  not not_13 (not_13_out, Opcode[0]);
  not not_14 (not_14_out, Opcode[3]);
  not not_15 (not_15_out, Opcode[2]);
  not not_16 (not_16_out, Opcode[3]);
  not not_17 (not_17_out, Opcode[1]);
  not not_18 (not_18_out, Opcode[0]);
  not not_19 (not_19_out, Opcode[2]);
  not not_20 (not_20_out, Opcode[2]);
  not not_21 (not_21_out, Opcode[1]);
  not not_22 (not_22_out, Opcode[1]);
  not not_23 (not_23_out, Opcode[0]);
  not not_24 (not_24_out, Opcode[1]);
  not not_25 (not_25_out, Opcode[3]);
  not not_26 (not_26_out, Opcode[2]);
  not not_27 (not_27_out, Opcode[1]);
  and and_1 (and_1_out, not_1_out, Opcode[2], Opcode[0]);
  and and_2 (and_2_out, not_2_out, Opcode[2], Opcode[1]);
  and and_3 (and_3_out, Opcode[3], not_3_out, not_4_out, not_5_out);
  and and_4 (MemRead, Opcode[3], Opcode[2], not_6_out, not_7_out, not_8_out);
  and and_5 (MemtoReg, Opcode[3], not_9_out, not_10_out);
  and and_6 (Halt, Opcode[3], not_11_out, Opcode[1], Opcode[0]);
  and and_7 (MemWrite, Opcode[3], Opcode[2], not_12_out, not_13_out, SubOp);
  and and_8 (and_8_out, not_14_out, not_15_out);
  and and_9 (and_9_out, not_16_out, not_17_out, not_18_out);
  and and_10 (and_10_out, not_19_out, Opcode[0]);
  and and_11 (and_11_out, not_20_out, Opcode[1]);
  and and_12 (and_12_out, Opcode[3], Opcode[2]);
  and and_13 (and_13_out, Opcode[3], not_21_out, Opcode[0]);
  and and_14 (and_14_out, Opcode[3], Opcode[2], not_22_out, not_23_out);
  and and_15 (and_15_out, Opcode[3], Opcode[2], Opcode[1], not_28_out);
  not not_28 (not_28_out, Opcode[0]);
  and and_16 (and_16_out, not_24_out, SubOp, Opcode[0]);
  and and_17 (and_17_out, Opcode[2], Opcode[0]);
  and and_18 (and_18_out, not_25_out, Opcode[2], Opcode[1]);
  and and_19 (and_19_out, Opcode[3], not_26_out, not_27_out);
  or or_1 (Branch, and_1_out, and_2_out, and_3_out);
  or or_2 (RegWrite, and_8_out, and_9_out, and_10_out, and_11_out, and_12_out);
  or or_3 (ALUSrc, and_13_out, and_14_out, and_15_out);
  or or_4 (Immed, and_16_out, and_17_out, and_18_out, and_19_out);
  not not_29 (not_29_out, a2);
  not not_30 (not_30_out, a2);
  not not_31 (not_31_out, subop_2);
  not not_32 (not_32_out, a3);
  and and_20 (and_20_out, a0, not_29_out, a3);
  and and_21 (and_21_out, a0, a1, not_30_out, not_31_out);
  and and_22 (and_22_out, a0, a1, a2, not_32_out);
  or or_5 (jump, and_20_out, and_21_out, and_22_out);
endmodule

module PutControl (
  input  [3:0] Opcode,
  output Put
);

  wire not_1_out;

  not not_1 (not_1_out, Opcode[2]);
  and and_1 (Put, Opcode[3], not_1_out, Opcode[1]);
endmodule

module ImmControl (
  input  [3:0] Opcode,
  input  subop,
  output immed
);

  wire and_1_out, and_2_out, and_3_out, and_4_out, not_1_out, not_2_out, not_3_out, not_4_out;

  not not_1 (not_1_out, Opcode[1]);
  not not_2 (not_2_out, Opcode[3]);
  not not_3 (not_3_out, Opcode[2]);
  not not_4 (not_4_out, Opcode[1]);
  and and_1 (and_1_out, not_1_out, Opcode[0], subop);
  and and_2 (and_2_out, Opcode[2], Opcode[0]);
  and and_3 (and_3_out, not_2_out, Opcode[2], Opcode[1]);
  and and_4 (and_4_out, Opcode[3], not_3_out, not_4_out);
  or or_1 (immed, and_1_out, and_2_out, and_3_out, and_4_out);
endmodule

module multControl (
  input  [3:0] Opcode,
  input  subop,
  output multcontrol
);

  wire not_1_out, not_2_out;

  not not_1 (not_1_out, Opcode[3]);
  not not_2 (not_2_out, Opcode[2]);
  and and_1 (multcontrol, not_1_out, not_2_out, Opcode[1], Opcode[0], subop);
endmodule

module Hi_Control (
  input  [3:0] Opcode,
  input  subop,
  output Hi
);

  wire not_1_out, not_2_out, not_3_out;

  not not_1 (not_1_out, Opcode[3]);
  not not_2 (not_2_out, Opcode[1]);
  not not_3 (not_3_out, Opcode[0]);
  and and_1 (Hi, not_1_out, Opcode[2], not_2_out, not_3_out, subop);
endmodule

module Hi_Low_Control (
  input  [3:0] Opcode,
  input  subop,
  output Hi
);

  wire not_1_out, not_2_out, not_3_out;

  not not_1 (not_1_out, Opcode[3]);
  not not_2 (not_2_out, Opcode[1]);
  not not_3 (not_3_out, Opcode[0]);
  and and_1 (Hi, not_1_out, Opcode[2], not_2_out, not_3_out);
endmodule

module mult_divcontrol (
  input  [3:0] Opcode,
  output multcontrol
);

  wire not_1_out, not_2_out;

  not not_1 (not_1_out, Opcode[3]);
  not not_2 (not_2_out, Opcode[2]);
  and and_1 (multcontrol, not_1_out, not_2_out, Opcode[1], Opcode[0]);
endmodule

module ImmedControl (
  input  [3:0] Opcode,
  output immed
);

  wire and_1_out, and_2_out, and_3_out, not_1_out, not_2_out, not_3_out;

  not not_1 (not_1_out, Opcode[3]);
  not not_2 (not_2_out, Opcode[2]);
  not not_3 (not_3_out, Opcode[1]);
  and and_1 (and_1_out, not_1_out, Opcode[2]);
  and and_2 (and_2_out, Opcode[2], Opcode[0]);
  and and_3 (and_3_out, Opcode[3], not_2_out, not_3_out);
  or or_1 (immed, and_1_out, and_2_out, and_3_out);
endmodule

module BranchControl (
  input  [3:0] Opcode,
  output bp,
  output bn,
  output bx,
  output bz
);

  wire not_1_out, not_2_out, not_3_out, not_4_out, not_5_out, not_6_out, not_7_out, not_8_out;

  not not_1 (not_1_out, Opcode[3]);
  not not_2 (not_2_out, Opcode[1]);
  not not_3 (not_3_out, Opcode[3]);
  not not_4 (not_4_out, Opcode[0]);
  not not_5 (not_5_out, Opcode[3]);
  not not_6 (not_6_out, Opcode[2]);
  not not_7 (not_7_out, Opcode[1]);
  not not_8 (not_8_out, Opcode[0]);
  and and_1 (bp, not_1_out, Opcode[2], not_2_out, Opcode[0]);
  and and_2 (bn, not_3_out, Opcode[2], Opcode[1], not_4_out);
  and and_3 (bx, not_5_out, Opcode[2], Opcode[1], Opcode[0]);
  and and_4 (bz, Opcode[3], not_6_out, not_7_out, not_8_out);
endmodule

module JumpControl (
  input  [3:0] Opcode,
  output jump
);

  wire and_1_out, and_2_out, not_1_out, not_2_out;

  not not_1 (not_1_out, Opcode[1]);
  not not_2 (not_2_out, Opcode[0]);
  and and_1 (and_1_out, Opcode[3], not_1_out, Opcode[0]);
  and and_2 (and_2_out, Opcode[3], Opcode[2], Opcode[1], not_2_out);
  or or_1 (jump, and_1_out, and_2_out);
endmodule

module JRControl (
  input  [3:0] Opcode,
  output jump
);

  wire not_1_out;

  not not_1 (not_1_out, Opcode[0]);
  and and_1 (jump, Opcode[3], Opcode[2], Opcode[1], not_1_out);
endmodule

module JALControl (
  input  [3:0] Opcode,
  output jump
);

  wire not_1_out, not_2_out;

  not not_1 (not_1_out, Opcode[2]);
  not not_2 (not_2_out, Opcode[1]);
  and and_1 (jump, Opcode[3], not_1_out, not_2_out, Opcode[0]);
endmodule

module SWControl (
  input  [3:0] Opcode,
  output ALUSrc
);

  wire not_1_out, not_2_out;

  not not_1 (not_1_out, Opcode[1]);
  not not_2 (not_2_out, Opcode[0]);
  and and_1 (ALUSrc, Opcode[3], Opcode[2], not_1_out, not_2_out);
endmodule

module ALUSrcControl (
  input  [3:0] Opcode,
  input  subop,
  output alusrc
);

  wire and_1_out, and_2_out, not_1_out, not_2_out, not_3_out, not_4_out, not_5_out, not_6_out;

  not not_1 (not_1_out, Opcode[3]);
  not not_2 (not_2_out, Opcode[2]);
  not not_3 (not_3_out, Opcode[1]);
  not not_4 (not_4_out, Opcode[1]);
  not not_5 (not_5_out, Opcode[0]);
  not not_6 (not_6_out, subop);
  and and_1 (and_1_out, not_1_out, not_2_out, not_3_out, Opcode[0]);
  and and_2 (and_2_out, Opcode[3], Opcode[2], not_4_out, not_5_out, not_6_out);
  or or_1 (alusrc, and_1_out, and_2_out);
endmodule

module adduiControl (
  input  [3:0] Opcode,
  input  subop,
  output addui
);

  wire not_1_out, not_2_out, not_3_out, not_4_out;

  not not_1 (not_1_out, Opcode[3]);
  not not_2 (not_2_out, Opcode[2]);
  not not_3 (not_3_out, Opcode[1]);
  not not_4 (not_4_out, subop);
  and and_1 (addui, not_1_out, not_2_out, not_3_out, Opcode[0], not_4_out);
endmodule
